# Fritzing sketch analog_board (saved by Fritzing 0.9.0b)
breadboards: 1

parts:
  IC1 = CD22M3494 [package=THT]
  IC2 = AD8403 [package=TSSOP]
  IN01 = female pin header, 2 pins [form="♀ (female)"]
  IN02 = female pin header, 2 pins [form="♀ (female)"]
  IC3 = AD8403 [package=TSSOP]
  IN03 = female pin header, 2 pins [form="♀ (female)"]
  IN04 = female pin header, 2 pins [form="♀ (female)"]
  IC5 = AD8403 [package=TSSOP]
  IC4 = AD8403 [package=TSSOP]
  IN5 = female pin header, 2 pins [form="♀ (female)"]
  IN6 = female pin header, 2 pins [form="♀ (female)"]
  IN7 = female pin header, 2 pins [form="♀ (female)"]
  IN8 = female pin header, 2 pins [form="♀ (female)"]
  IC6 = CD22M3494 [package=THT]
  IN9 = female pin header, 2 pins [form="♀ (female)"]
  IN10 = female pin header, 2 pins [form="♀ (female)"]
  IN11 = female pin header, 2 pins [form="♀ (female)"]
  IN12 = female pin header, 2 pins [form="♀ (female)"]
  IN13 = female pin header, 2 pins [form="♀ (female)"]
  IN14 = female pin header, 2 pins [form="♀ (female)"]
  IN15 = female pin header, 2 pins [form="♀ (female)"]
  IN16 = female pin header, 2 pins [form="♀ (female)"]

nets:
  N1: IC1.Y1#0, IN14.pin2
  N2: IC1.X14, IC4.22, IC6.X14
  N3: IC1.X15, IC4.4, IC6.X15
  N4: IC1.X6, IC4.18, IC6.X6
  N5: IC1.X7, IC4.8, IC6.X7
  N6: IC1.X8, IC5.22, IC6.X8
  N7: IC1.X9, IC1.X1, IC2.4, IC5.4, IC6.X9, IC6.X1
  N8: IC1.X10, IC1.X2, IC2.18, IC5.18, IC6.X10, IC6.X2
  N9: IC1.X11, IC5.8, IC6.X11
  N10: IC1.Y7, IN16.pin2
  N11: IC1.Y6, IN16.pin1
  N12: IC1.Y5, IN13.pin2
  N13: IC1.Y4, IN13.pin1
  N14: IC1.X13, IC3.8, IC6.X13
  N15: IC1.X12, IC3.18, IC6.X12
  N16: IC1.X5, IC3.4, IC6.X5
  N17: IC1.X4, IC3.22, IC6.X4
  N18: IC1.X3, IC2.8, IC6.X3
  N19: IC1.X0, IC2.22, IC6.X0
  N20: IC1.Y0, IN15.pin1
  N21: IC1.Y1#36, IN15.pin2
  N22: IC1.Y2, IN14.pin1
  GND: IC2.1, IC2.5, IC2.9, IC2.17, IC2.21, IC3.1, IC3.5, IC3.9, IC3.17, IC3.21, IC5.1, IC5.5, IC5.9, IC5.17, IC5.21, IC4.1, IC4.5, IC4.9, IC4.17, IC4.21
  N23: IC2.3, IN01.pin1
  N24: IC2.7, IN01.pin2
  5V: IC2.16, IC3.16, IC5.16, IC4.16
  N25: IC2.19, IN02.pin2
  N26: IC2.23, IN02.pin1
  N27: IC3.3, IN03.pin1
  N28: IC3.7, IN03.pin2
  N29: IC3.19, IN04.pin2
  N30: IC3.23, IN04.pin1
  N31: IC5.3, IN6.pin1
  N32: IC5.7, IN6.pin2
  N33: IC5.19, IN7.pin2
  N34: IC5.23, IN7.pin1
  N35: IC4.3, IN5.pin1
  N36: IC4.7, IN5.pin2
  N37: IC4.19, IN8.pin2
  N38: IC4.23, IN8.pin1
  N39: IC6.Y1#0, IN10.pin2
  N40: IC6.Y7, IN12.pin2
  N41: IC6.Y6, IN12.pin1
  N42: IC6.Y5, IN11.pin2
  N43: IC6.Y4, IN11.pin1
  N44: IC6.Y0, IN9.pin1
  N45: IC6.Y1#36, IN9.pin2
  N46: IC6.Y2, IN10.pin1

custom parts:
  CD22M3494: CD22M3494 from Intersil http://www.icbase.com/pdf/ITS/ITS14170701.pdf
  AD8403: http://www.analog.com/static/imported-files/data_sheets/AD8400_8402_8403.pdf
