# Fritzing sketch arduino_shield (saved by Fritzing 0.9.0b)
breadboards: 1

parts:
  PDU = female pin header, 8 pins [form="♀ (female)"]
  J2 = female pin header, 8 pins [form="♀ (female)"]  # not connected
  J3 = female pin header, 8 pins [form="♀ (female)"]  # not connected
  J4 = female pin header, 8 pins [form="♀ (female)"]  # not connected
  I2C_JUMPERS = female pin header, 8 pins [form="♀ (female)"]
  J7 = female pin header, 10 pins [form="♀ (female)"]
  SWITCH_CTRL = double row female pin header, 16 pins [form="♀ (female)"]
  POT_CTRL = double row female pin header, 16 pins [form="♀ (female)"]
  SPI_JUMPERS = double row female pin header, 36 pins [form="♀ (female)"]
  TOP_SHIFT_REGISTER = MCP23017 I2C I/O Expander
  TOP = double row female pin header, 16 pins [form="♀ (female)"]
  BOTTOM = double row female pin header, 16 pins [form="♀ (female)"]
  R1 = Resistor [tolerance=±5% resistance=10k package=THT]
  R2 = Resistor [tolerance=±5% resistance=10k package=THT]
  R3 = Resistor [tolerance=±5% resistance=220 package=THT]
  R4 = Resistor [tolerance=±5% resistance=220 package=THT]
  R5 = Resistor [tolerance=±5% resistance=220 package=THT]
  R6 = Resistor [tolerance=±5% resistance=220 package=THT]
  R7 = Resistor [tolerance=±5% resistance=220 package=THT]
  R8 = Resistor [tolerance=±5% resistance=220 package=THT]
  R10 = Resistor [tolerance=±5% resistance=220 package=THT]
  R9 = Resistor [tolerance=±5% resistance=220 package=THT]
  R11 = Resistor [tolerance=±5% resistance=220 package=THT]
  R12 = Resistor [tolerance=±5% resistance=220 package=THT]
  R13 = Resistor [tolerance=±5% resistance=220 package=THT]
  R14 = Resistor [tolerance=±5% resistance=220 package=THT]
  R15 = Resistor [tolerance=±5% resistance=220 package=THT]
  R16 = Resistor [tolerance=±5% resistance=220 package=THT]
  R17 = Resistor [tolerance=±5% resistance=220 package=THT]
  R18 = Resistor [tolerance=±5% resistance=220 package=THT]
  R19 = Resistor [tolerance=±5% resistance=220 package=THT]
  R26 = Resistor [tolerance=±5% resistance=220 package=THT]
  R31 = Resistor [tolerance=±5% resistance=220 package=THT]
  R22 = Resistor [tolerance=±5% resistance=220 package=THT]
  R25 = Resistor [tolerance=±5% resistance=220 package=THT]
  R29 = Resistor [tolerance=±5% resistance=220 package=THT]
  R23 = Resistor [tolerance=±5% resistance=220 package=THT]
  R24 = Resistor [tolerance=±5% resistance=220 package=THT]
  R33 = Resistor [tolerance=±5% resistance=220 package=THT]
  R21 = Resistor [tolerance=±5% resistance=220 package=THT]
  R30 = Resistor [tolerance=±5% resistance=220 package=THT]
  R27 = Resistor [tolerance=±5% resistance=220 package=THT]
  R22_2 = Resistor [tolerance=±5% resistance=220 package=THT]
  R32 = Resistor [tolerance=±5% resistance=220 package=THT]
  R20 = Resistor [tolerance=±5% resistance=220 package=THT]
  R28 = Resistor [tolerance=±5% resistance=220 package=THT]
  BOTTOM_SHIFT_REGISTER = MCP23017 I2C I/O Expander
  I2C = female pin header, 2 pins [form="♀ (female)"]

nets:
  GND: PDU.pin2, PDU.pin3, J7.pin7, SWITCH_CTRL.pin16, TOP_SHIFT_REGISTER.VSS, TOP_SHIFT_REGISTER.A0, TOP_SHIFT_REGISTER.A1, TOP_SHIFT_REGISTER.A2, BOTTOM_SHIFT_REGISTER.VSS, BOTTOM_SHIFT_REGISTER.A1, BOTTOM_SHIFT_REGISTER.A2
  5V: PDU.pin4, POT_CTRL.pin9, TOP_SHIFT_REGISTER.VDD, R2.Pin_1, BOTTOM_SHIFT_REGISTER.VDD, BOTTOM_SHIFT_REGISTER.A0
  N1: I2C_JUMPERS.pin1, TOP_SHIFT_REGISTER.SCL, BOTTOM_SHIFT_REGISTER.SCL, I2C.pin2
  N2: I2C_JUMPERS.pin2, TOP_SHIFT_REGISTER.SDA, BOTTOM_SHIFT_REGISTER.SDA, I2C.pin1
  N3: SWITCH_CTRL.pin1, SPI_JUMPERS.pin29
  N4: SWITCH_CTRL.pin2, SPI_JUMPERS.pin28
  N5: SWITCH_CTRL.pin3, SPI_JUMPERS.pin27
  N6: SWITCH_CTRL.pin4, SPI_JUMPERS.pin26
  N7: SWITCH_CTRL.pin5, SPI_JUMPERS.pin25
  N8: SWITCH_CTRL.pin6, SPI_JUMPERS.pin24
  N9: SWITCH_CTRL.pin7, SPI_JUMPERS.pin23
  N10: SWITCH_CTRL.pin8, SPI_JUMPERS.pin22
  N11: SWITCH_CTRL.pin9, SPI_JUMPERS.pin19
  N12: SWITCH_CTRL.pin10, POT_CTRL.pin10, SPI_JUMPERS.pin36
  N13: SWITCH_CTRL.pin11, SPI_JUMPERS.pin13
  N14: SWITCH_CTRL.pin12, SPI_JUMPERS.pin12
  N15: SWITCH_CTRL.pin13, SPI_JUMPERS.pin11
  N16: SWITCH_CTRL.pin14, SPI_JUMPERS.pin10
  N17: SWITCH_CTRL.pin15, SPI_JUMPERS.pin9
  N18: POT_CTRL.pin1, SPI_JUMPERS.pin3
  N19: POT_CTRL.pin2, SPI_JUMPERS.pin5
  N20: POT_CTRL.pin3, SPI_JUMPERS.pin32
  N21: POT_CTRL.pin4, SPI_JUMPERS.pin7
  N22: POT_CTRL.pin5, SPI_JUMPERS.pin30
  N23: POT_CTRL.pin12, SPI_JUMPERS.pin31
  N24: POT_CTRL.pin13, SPI_JUMPERS.pin6
  N25: POT_CTRL.pin14, SPI_JUMPERS.pin33
  N26: POT_CTRL.pin15, SPI_JUMPERS.pin4
  N27: POT_CTRL.pin16, SPI_JUMPERS.pin35
  N28: SPI_JUMPERS.pin18, R1.Pin_1
  N29: TOP_SHIFT_REGISTER.GPB0, R11.Pin_1
  N30: TOP_SHIFT_REGISTER.GPB1, R12.Pin_1
  N31: TOP_SHIFT_REGISTER.GPB2, R13.Pin_1
  N32: TOP_SHIFT_REGISTER.GPB3, R14.Pin_1
  N33: TOP_SHIFT_REGISTER.GPB4, R15.Pin_1
  N34: TOP_SHIFT_REGISTER.GPB5, R16.Pin_1
  N35: TOP_SHIFT_REGISTER.GPB6, R17.Pin_1
  N36: TOP_SHIFT_REGISTER.GPB7, R18.Pin_1
  N37: TOP_SHIFT_REGISTER.RESET, R1.Pin_0
  N38: TOP_SHIFT_REGISTER.GPA0, R3.Pin_1
  N39: TOP_SHIFT_REGISTER.GPA1, R4.Pin_1
  N40: TOP_SHIFT_REGISTER.GPA2, R5.Pin_1
  N41: TOP_SHIFT_REGISTER.GPA3, R6.Pin_1
  N42: TOP_SHIFT_REGISTER.GPA4, R7.Pin_1
  N43: TOP_SHIFT_REGISTER.GPA5, R8.Pin_1
  N44: TOP_SHIFT_REGISTER.GPA6, R9.Pin_1
  N45: TOP_SHIFT_REGISTER.GPA7, R10.Pin_1
  N46: TOP.pin1, R10.Pin_0
  N47: TOP.pin2, R9.Pin_0
  N48: TOP.pin3, R8.Pin_0
  N49: TOP.pin4, R7.Pin_0
  N50: TOP.pin5, R6.Pin_0
  N51: TOP.pin6, R5.Pin_0
  N52: TOP.pin7, R4.Pin_0
  N53: TOP.pin8, R3.Pin_0
  N54: TOP.pin9, R18.Pin_0
  N55: TOP.pin10, R17.Pin_0
  N56: TOP.pin11, R16.Pin_0
  N57: TOP.pin12, R15.Pin_0
  N58: TOP.pin13, R14.Pin_0
  N59: TOP.pin14, R13.Pin_0
  N60: TOP.pin15, R12.Pin_0
  N61: TOP.pin16, R11.Pin_0
  N62: BOTTOM.pin1, R25.Pin_0
  N63: BOTTOM.pin2, R24.Pin_0
  N64: BOTTOM.pin3, R23.Pin_0
  N65: BOTTOM.pin4, R22_2.Pin_0
  N66: BOTTOM.pin5, R22.Pin_0
  N67: BOTTOM.pin6, R21.Pin_0
  N68: BOTTOM.pin7, R20.Pin_0
  N69: BOTTOM.pin8, R19.Pin_0
  N70: BOTTOM.pin9, R33.Pin_0
  N71: BOTTOM.pin10, R32.Pin_0
  N72: BOTTOM.pin11, R31.Pin_0
  N73: BOTTOM.pin12, R30.Pin_0
  N74: BOTTOM.pin13, R29.Pin_0
  N75: BOTTOM.pin14, R28.Pin_0
  N76: BOTTOM.pin15, R27.Pin_0
  N77: BOTTOM.pin16, R26.Pin_0
  N78: R2.Pin_0, BOTTOM_SHIFT_REGISTER.RESET
  N79: R19.Pin_1, BOTTOM_SHIFT_REGISTER.GPA0
  N80: R26.Pin_1, BOTTOM_SHIFT_REGISTER.GPB0
  N81: R31.Pin_1, BOTTOM_SHIFT_REGISTER.GPB5
  N82: R22.Pin_1, BOTTOM_SHIFT_REGISTER.GPA3
  N83: R25.Pin_1, BOTTOM_SHIFT_REGISTER.GPA7
  N84: R29.Pin_1, BOTTOM_SHIFT_REGISTER.GPB3
  N85: R23.Pin_1, BOTTOM_SHIFT_REGISTER.GPA5
  N86: R24.Pin_1, BOTTOM_SHIFT_REGISTER.GPA6
  N87: R33.Pin_1, BOTTOM_SHIFT_REGISTER.GPB7
  N88: R21.Pin_1, BOTTOM_SHIFT_REGISTER.GPA2
  N89: R30.Pin_1, BOTTOM_SHIFT_REGISTER.GPB4
  N90: R27.Pin_1, BOTTOM_SHIFT_REGISTER.GPB1
  N91: R22_2.Pin_1, BOTTOM_SHIFT_REGISTER.GPA4
  N92: R32.Pin_1, BOTTOM_SHIFT_REGISTER.GPB6
  N93: R20.Pin_1, BOTTOM_SHIFT_REGISTER.GPA1
  N94: R28.Pin_1, BOTTOM_SHIFT_REGISTER.GPB2

notes:
  SDA
  SCL
  GND
  5V
  3V3
  50
  51
  52
  53

custom parts:
  MCP23017 I2C I/O Expander: MCP23017 I2C 16-Channel I/O Expander
