# Fritzing sketch led_output_board (saved by Fritzing 0.9.0b)
circuit board: 15.9339cm x 9.33155cm
breadboards: 1

parts:
  U1 = 74HC595 [package="DIP16 [THT]"]
  U2 = 74HC595 [package="DIP16 [THT]"]
  J1 = shrouded pin header, 10 pins [form="♂ (shrouded male)"]
  R1 = Resistor [tolerance=±5% resistance=220 package=THT]
  R2 = Resistor [tolerance=±5% resistance=220 package=THT]
  R3 = Resistor [tolerance=±5% resistance=220 package=THT]
  R4 = Resistor [tolerance=±5% resistance=220 package=THT]
  R5 = Resistor [tolerance=±5% resistance=220 package=THT]
  R6 = Resistor [tolerance=±5% resistance=220 package=THT]
  R7 = Resistor [tolerance=±5% resistance=220 package=THT]
  R8 = Resistor [tolerance=±5% resistance=220 package=THT]
  R9 = Resistor [tolerance=±5% resistance=220 package=THT]
  R10 = Resistor [tolerance=±5% resistance=220 package=THT]
  R11 = Resistor [tolerance=±5% resistance=220 package=THT]
  R12 = Resistor [tolerance=±5% resistance=220 package=THT]
  R13 = Resistor [tolerance=±5% resistance=220 package=THT]
  R14 = Resistor [tolerance=±5% resistance=220 package=THT]
  R15 = Resistor [tolerance=±5% resistance=220 package=THT]
  R16 = Resistor [tolerance=±5% resistance=220 package=THT]
  U3 = 74HC595 [package="DIP16 [THT]"]
  U4 = 74HC595 [package="DIP16 [THT]"]
  U5 = 74HC595 [package="DIP16 [THT]"]
  U6 = 74HC595 [package="DIP16 [THT]"]
  J2 = shrouded pin header, 16 pins [form="♂ (shrouded male)"]
  R17 = Resistor [tolerance=±5% resistance=220 package=THT]
  R18 = Resistor [tolerance=±5% resistance=220 package=THT]
  R19 = Resistor [tolerance=±5% resistance=220 package=THT]
  R20 = Resistor [tolerance=±5% resistance=220 package=THT]
  R21 = Resistor [tolerance=±5% resistance=220 package=THT]
  R22 = Resistor [tolerance=±5% resistance=220 package=THT]
  R23 = Resistor [tolerance=±5% resistance=220 package=THT]
  R24 = Resistor [tolerance=±5% resistance=220 package=THT]
  R25 = Resistor [tolerance=±5% resistance=220 package=THT]
  R26 = Resistor [tolerance=±5% resistance=220 package=THT]
  R27 = Resistor [tolerance=±5% resistance=220 package=THT]
  R28 = Resistor [tolerance=±5% resistance=220 package=THT]
  R29 = Resistor [tolerance=±5% resistance=220 package=THT]
  R30 = Resistor [tolerance=±5% resistance=220 package=THT]
  R31 = Resistor [tolerance=±5% resistance=220 package=THT]
  R32 = Resistor [tolerance=±5% resistance=220 package=THT]
  J3 = shrouded pin header, 16 pins [form="♂ (shrouded male)"]
  R33 = Resistor [tolerance=±5% resistance=220 package=THT]
  R34 = Resistor [tolerance=±5% resistance=220 package=THT]
  R35 = Resistor [tolerance=±5% resistance=220 package=THT]
  R36 = Resistor [tolerance=±5% resistance=220 package=THT]
  R37 = Resistor [tolerance=±5% resistance=220 package=THT]
  R38 = Resistor [tolerance=±5% resistance=220 package=THT]
  R39 = Resistor [tolerance=±5% resistance=220 package=THT]
  R40 = Resistor [tolerance=±5% resistance=220 package=THT]
  R41 = Resistor [tolerance=±5% resistance=220 package=THT]
  R42 = Resistor [tolerance=±5% resistance=220 package=THT]
  R43 = Resistor [tolerance=±5% resistance=220 package=THT]
  R44 = Resistor [tolerance=±5% resistance=220 package=THT]
  R45 = Resistor [tolerance=±5% resistance=220 package=THT]
  R46 = Resistor [tolerance=±5% resistance=220 package=THT]
  R47 = Resistor [tolerance=±5% resistance=220 package=THT]
  R48 = Resistor [tolerance=±5% resistance=220 package=THT]
  J4 = shrouded pin header, 16 pins [form="♂ (shrouded male)"]
  C1 = Tantalum Capacitor [capacitance=1μF package="100 mil [THT, tantalum]"]
  C2 = Tantalum Capacitor [capacitance=1μF package="100 mil [THT, tantalum]"]
  C3 = Tantalum Capacitor [capacitance=1μF package="100 mil [THT, tantalum]"]

nets:
  N1: U1.Q1, R2.Pin_1
  N2: U1.Q2, R3.Pin_1
  N3: U1.Q3, R4.Pin_1
  N4: U1.Q4, R5.Pin_1
  N5: U1.Q5, R6.Pin_1
  N6: U1.Q6, R7.Pin_1
  N7: U1.Q7, R8.Pin_1
  GND: U1.GND, U1.OE, U2.GND, U2.OE, U3.GND, U3.OE, U4.GND, U4.OE, U5.GND, U5.OE, U6.GND, U6.OE, C1.-, C2.-, C3.-
  N8: U1.Q7', U2.DS
  VCC: U1.MR, U1.VCC, U2.MR, U2.VCC, J1.pin10, U3.MR, U3.VCC, U4.MR, U4.VCC, U5.MR, U5.VCC, U6.MR, U6.VCC
  N9: U1.SH_CP, U2.SH_CP, J1.pin3
  N10: U1.ST_CP, U2.ST_CP, J1.pin2, C3.+
  N11: U1.DS, J1.pin1
  N12: U1.Q0, R1.Pin_1
  N13: U2.Q1, R10.Pin_1
  N14: U2.Q2, R11.Pin_1
  N15: U2.Q3, R12.Pin_1
  N16: U2.Q4, R13.Pin_1
  N17: U2.Q5, R14.Pin_1
  N18: U2.Q6, R15.Pin_1
  N19: U2.Q7, R16.Pin_1
  N20: U2.Q0, R9.Pin_1
  N21: J1.pin4, U3.DS
  N22: J1.pin5, U3.ST_CP, U4.ST_CP, C2.+
  N23: J1.pin6, U3.SH_CP, U4.SH_CP
  N24: J1.pin7, U5.DS
  N25: J1.pin8, U5.ST_CP, U6.ST_CP, C1.+
  N26: J1.pin9, U5.SH_CP, U6.SH_CP
  N27: R1.Pin_0, J2.pin16
  N28: R2.Pin_0, J2.pin15
  N29: R3.Pin_0, J2.pin14
  N30: R4.Pin_0, J2.pin13
  N31: R5.Pin_0, J2.pin12
  N32: R6.Pin_0, J2.pin11
  N33: R7.Pin_0, J2.pin10
  N34: R8.Pin_0, J2.pin9
  N35: R9.Pin_0, J2.pin8
  N36: R10.Pin_0, J2.pin7
  N37: R11.Pin_0, J2.pin6
  N38: R12.Pin_0, J2.pin5
  N39: R13.Pin_0, J2.pin4
  N40: R14.Pin_0, J2.pin3
  N41: R15.Pin_0, J2.pin2
  N42: R16.Pin_0, J2.pin1
  N43: U3.Q1, R24.Pin_1
  N44: U3.Q2, R29.Pin_1
  N45: U3.Q3, R25.Pin_1
  N46: U3.Q4, R18.Pin_1
  N47: U3.Q5, R28.Pin_1
  N48: U3.Q6, R22.Pin_1
  N49: U3.Q7, R26.Pin_1
  N50: U3.Q7', U4.DS
  N51: U3.Q0, R27.Pin_1
  N52: U4.Q1, R19.Pin_1
  N53: U4.Q2, R32.Pin_1
  N54: U4.Q3, R31.Pin_1
  N55: U4.Q4, R30.Pin_1
  N56: U4.Q5, R17.Pin_1
  N57: U4.Q6, R20.Pin_1
  N58: U4.Q7, R23.Pin_1
  N59: U4.Q0, R21.Pin_1
  N60: U5.Q1, R40.Pin_1
  N61: U5.Q2, R45.Pin_1
  N62: U5.Q3, R41.Pin_1
  N63: U5.Q4, R34.Pin_1
  N64: U5.Q5, R44.Pin_1
  N65: U5.Q6, R38.Pin_1
  N66: U5.Q7, R42.Pin_1
  N67: U5.Q7', U6.DS
  N68: U5.Q0, R43.Pin_1
  N69: U6.Q1, R39.Pin_1
  N70: U6.Q2, R48.Pin_1
  N71: U6.Q3, R47.Pin_1
  N72: U6.Q4, R46.Pin_1
  N73: U6.Q5, R33.Pin_1
  N74: U6.Q6, R36.Pin_1
  N75: U6.Q7, R35.Pin_1
  N76: U6.Q0, R37.Pin_1
  N77: R17.Pin_0, J3.pin3
  N78: R18.Pin_0, J3.pin12
  N79: R19.Pin_0, J3.pin7
  N80: R20.Pin_0, J3.pin2
  N81: R21.Pin_0, J3.pin8
  N82: R22.Pin_0, J3.pin10
  N83: R23.Pin_0, J3.pin1
  N84: R24.Pin_0, J3.pin15
  N85: R25.Pin_0, J3.pin13
  N86: R26.Pin_0, J3.pin9
  N87: R27.Pin_0, J3.pin16
  N88: R28.Pin_0, J3.pin11
  N89: R29.Pin_0, J3.pin14
  N90: R30.Pin_0, J3.pin4
  N91: R31.Pin_0, J3.pin5
  N92: R32.Pin_0, J3.pin6
  N93: R33.Pin_0, J4.pin3
  N94: R34.Pin_0, J4.pin12
  N95: R35.Pin_0, J4.pin1
  N96: R36.Pin_0, J4.pin2
  N97: R37.Pin_0, J4.pin8
  N98: R38.Pin_0, J4.pin10
  N99: R39.Pin_0, J4.pin7
  N100: R40.Pin_0, J4.pin15
  N101: R41.Pin_0, J4.pin13
  N102: R42.Pin_0, J4.pin9
  N103: R43.Pin_0, J4.pin16
  N104: R44.Pin_0, J4.pin11
  N105: R45.Pin_0, J4.pin14
  N106: R46.Pin_0, J4.pin4
  N107: R47.Pin_0, J4.pin5
  N108: R48.Pin_0, J4.pin6
