# Fritzing sketch led_output_board_v2 (saved by Fritzing 0.9.0b)
circuit board: 7.22463cm x 7.60476cm
breadboards: 1

parts:
  U1 = 74HC595 [package="DIP16 [THT]"]
  R1 = Resistor [tolerance=±5% resistance=220 package=THT]
  R2 = Resistor [tolerance=±5% resistance=220 package=THT]
  R3 = Resistor [tolerance=±5% resistance=220 package=THT]
  R4 = Resistor [tolerance=±5% resistance=220 package=THT]
  R5 = Resistor [tolerance=±5% resistance=220 package=THT]
  R6 = Resistor [tolerance=±5% resistance=220 package=THT]
  R7 = Resistor [tolerance=±5% resistance=220 package=THT]
  R8 = Resistor [tolerance=±5% resistance=220 package=THT]
  R10 = Resistor [tolerance=±5% resistance=220 package=THT]
  R11 = Resistor [tolerance=±5% resistance=220 package=THT]
  R12 = Resistor [tolerance=±5% resistance=220 package=THT]
  R13 = Resistor [tolerance=±5% resistance=220 package=THT]
  R14 = Resistor [tolerance=±5% resistance=220 package=THT]
  R15 = Resistor [tolerance=±5% resistance=220 package=THT]
  R16 = Resistor [tolerance=±5% resistance=220 package=THT]
  J2 = shrouded pin header, 16 pins [form="♂ (shrouded male)"]
  U2 = 74HC595 [package="DIP16 [THT]"]
  R9 = Resistor [tolerance=±5% resistance=220 package=THT]
  J3 = female pin header, 3 pins [form="♀ (female)"]
  J4 = female pin header, 2 pins [form="♀ (female)"]
  J5 = female pin header, 2 pins [form="♀ (female)"]

nets:
  N1: U1.Q1, R2.Pin_1
  N2: U1.Q2, R3.Pin_1
  N3: U1.Q3, R4.Pin_1
  N4: U1.Q4, R5.Pin_1
  N5: U1.Q5, R6.Pin_1
  N6: U1.Q6, R7.Pin_1
  N7: U1.Q7, R8.Pin_1
  N8: U1.Q7', U2.DS
  N9: U1.SH_CP, U2.ST_CP, J3.pin3
  N10: U1.ST_CP, U2.SH_CP, J3.pin2
  GND: U1.OE, U2.OE
  N11: U1.DS, J3.pin1
  N12: U1.Q0, R1.Pin_1
  N13: R1.Pin_0, J2.pin16
  N14: R2.Pin_0, J2.pin15
  N15: R3.Pin_0, J2.pin14
  N16: R4.Pin_0, J2.pin13
  N17: R5.Pin_0, J2.pin12
  N18: R6.Pin_0, J2.pin11
  N19: R7.Pin_0, J2.pin10
  N20: R8.Pin_0, J2.pin9
  N21: R10.Pin_0, J2.pin7
  N22: R10.Pin_1, U2.Q1
  N23: R11.Pin_0, J2.pin6
  N24: R11.Pin_1, U2.Q2
  N25: R12.Pin_0, J2.pin5
  N26: R12.Pin_1, U2.Q3
  N27: R13.Pin_0, J2.pin4
  N28: R13.Pin_1, U2.Q4
  N29: R14.Pin_0, J2.pin3
  N30: R14.Pin_1, U2.Q5
  N31: R15.Pin_0, J2.pin2
  N32: R15.Pin_1, U2.Q6
  N33: R16.Pin_0, J2.pin1
  N34: R16.Pin_1, U2.Q7
  N35: J2.pin8, R9.Pin_0
  N36: U2.Q0, R9.Pin_1
  N37: J4.pin1, J5.pin1
  N38: J4.pin2, J5.pin2
